// Logisim project register_bank.circ as structural Verilog: 1 circuit, main circuit main
module main (
  input  [7:0] data,
  input  [1:0] opcode,
  input  [7:0] \var ,
  input  [1:0] delete,
  output [7:0] out_5
);

  wire clock_1_out, comparator_1_eq, comparator_3_eq, comparator_5_eq, comparator_7_eq, comparator_8_eq,
       comparator_9_eq, comparator_10_eq, comparator_11_eq, comparator_12_eq, comparator_13_eq,
       comparator_14_eq, demultiplexer_1_out1, demultiplexer_1_out2, demultiplexer_1_out3,
       demultiplexer_2_out1, demultiplexer_2_out3, demultiplexer_3_out1, demultiplexer_3_out2,
       demultiplexer_3_out3, not_1_out, not_2_out, not_3_out, not_4_out, not_5_out, not_6_out, not_7_out,
       not_8_out, not_9_out, not_10_out, not_11_out, not_12_out, not_13_out, pull_resistor_1_node,
       pull_resistor_2_node, pull_resistor_3_node;
  wire [1:0] pull_resistor_5_node, transistor_5_out, transistor_11_out;
  wire [2:0] comparator_2_eq;
  wire [7:0] register_1_q, register_2_q, register_3_q, register_4_q, register_5_q, register_6_q,
       transistor_1_out;

  Register register_1 (
    .D(\var ), .en(pull_resistor_1_node), .clk(clock_1_out), .Q(register_1_q), .clr(demultiplexer_1_out1));
  Register register_2 (
    .D(\var ), .en(pull_resistor_2_node), .clk(clock_1_out), .Q(register_2_q), .clr(demultiplexer_1_out2));
  Register register_3 (
    .D(\var ), .en(pull_resistor_3_node), .clk(clock_1_out), .Q(register_3_q), .clr(demultiplexer_1_out3));
  Clock clock_1 (.out(clock_1_out));
  Demultiplexer #(.select(2)) demultiplexer_1 (
    .out1(demultiplexer_1_out1), .out2(demultiplexer_1_out2), .out3(demultiplexer_1_out3), .in(1'b1),
    .sel(delete));  // open: out0
  Comparator comparator_1 (.a(register_1_q), .b(\var ), .eq(comparator_1_eq));  // open: gt, lt
  Comparator comparator_2 (.a(register_1_q), .b({8{1'b0}}), .eq(comparator_2_eq[0]));  // open: gt, lt
  Comparator comparator_3 (.a(register_2_q), .b(\var ), .eq(comparator_3_eq));  // open: gt, lt
  Comparator comparator_4 (.a(register_2_q), .b({8{1'b0}}), .eq(comparator_2_eq[1]));  // open: gt, lt
  Comparator comparator_5 (.a(register_3_q), .b(\var ), .eq(comparator_5_eq));  // open: gt, lt
  Comparator comparator_6 (.a(register_3_q), .b({8{1'b0}}), .eq(comparator_2_eq[2]));  // open: gt, lt
  not not_1 (not_1_out, comparator_1_eq);
  not not_2 (not_2_out, comparator_3_eq);
  not not_3 (not_3_out, comparator_5_eq);
  Pull_Resistor pull_resistor_1 (.node(pull_resistor_1_node));
  Pull_Resistor pull_resistor_2 (.node(pull_resistor_2_node));
  Pull_Resistor pull_resistor_3 (.node(pull_resistor_3_node));
  Register register_4 (
    .D(data), .en(pull_resistor_1_node), .clk(clock_1_out), .Q(register_4_q), .clr(demultiplexer_1_out1));
  Register register_5 (
    .D(data), .en(pull_resistor_2_node), .clk(clock_1_out), .Q(register_5_q), .clr(demultiplexer_1_out2));
  Register register_6 (
    .D(data), .en(pull_resistor_3_node), .clk(clock_1_out), .Q(register_6_q), .clr(demultiplexer_1_out3));
  Demultiplexer #(.select(2)) demultiplexer_2 (
    .out1(demultiplexer_2_out1), .out3(demultiplexer_2_out3), .in(1'b1), .sel(opcode));  // open: out0, out2
  Transistor #(.width(8)) transistor_1 (.in(register_4_q), .out(transistor_1_out), .gate(not_1_out));
  Transistor #(.width(8)) transistor_2 (.in(register_5_q), .out(transistor_1_out), .gate(not_2_out));
  Transistor #(.width(8)) transistor_3 (.in(transistor_1_out), .out(out_5), .gate(not_4_out));
  Transistor #(.width(8)) transistor_4 (.in(register_6_q), .out(transistor_1_out), .gate(not_3_out));
  Transistor #(.width(2)) transistor_5 (.in(2'b01), .out(transistor_5_out), .gate(not_1_out));
  Transistor #(.width(2)) transistor_6 (.in(2'b10), .out(transistor_5_out), .gate(not_2_out));
  Transistor #(.width(2)) transistor_7 (.in(2'b11), .out(transistor_5_out), .gate(not_3_out));
  Pull_Resistor pull_resistor_4 (.node(out_5));
  Transistor transistor_8 (.in(demultiplexer_3_out1), .out(pull_resistor_1_node), .gate(demultiplexer_2_out3));
  Transistor transistor_9 (.in(demultiplexer_3_out2), .out(pull_resistor_2_node), .gate(demultiplexer_2_out3));
  not not_4 (not_4_out, demultiplexer_2_out3);
  Demultiplexer #(.select(2)) demultiplexer_3 (
    .out1(demultiplexer_3_out1), .out2(demultiplexer_3_out2), .out3(demultiplexer_3_out3), .in(1'b1),
    .sel(pull_resistor_5_node));  // open: out0
  Transistor transistor_10 (.in(demultiplexer_3_out3), .out(pull_resistor_3_node), .gate(demultiplexer_2_out3));
  Comparator #(.width(3)) comparator_7 (.a(comparator_2_eq), .b(3'b111), .eq(comparator_7_eq));  // open: gt, lt
  Comparator #(.width(3)) comparator_8 (.a(comparator_2_eq), .b(3'b110), .eq(comparator_8_eq));  // open: gt, lt
  Comparator #(.width(3)) comparator_9 (.a(comparator_2_eq), .b(3'b101), .eq(comparator_9_eq));  // open: gt, lt
  Comparator #(.width(3)) comparator_10 (.a(comparator_2_eq), .b(3'b100), .eq(comparator_10_eq));  // open: gt, lt
  Comparator #(.width(3)) comparator_11 (.a(comparator_2_eq), .b(3'b011), .eq(comparator_11_eq));  // open: gt, lt
  Comparator #(.width(3)) comparator_12 (.a(comparator_2_eq), .b(3'b010), .eq(comparator_12_eq));  // open: gt, lt
  Comparator #(.width(3)) comparator_13 (.a(comparator_2_eq), .b(3'b001), .eq(comparator_13_eq));  // open: gt, lt
  Comparator #(.width(3)) comparator_14 (.a(comparator_2_eq), .b(3'b000), .eq(comparator_14_eq));  // open: gt, lt
  not not_5 (not_5_out, comparator_7_eq);
  Transistor #(.width(2)) transistor_11 (.in(2'b01), .out(transistor_11_out), .gate(not_5_out));
  not not_6 (not_6_out, comparator_8_eq);
  Transistor #(.width(2)) transistor_12 (.in(2'b10), .out(transistor_11_out), .gate(not_6_out));
  not not_7 (not_7_out, comparator_9_eq);
  Transistor #(.width(2)) transistor_13 (.in(2'b01), .out(transistor_11_out), .gate(not_7_out));
  not not_8 (not_8_out, comparator_10_eq);
  Transistor #(.width(2)) transistor_14 (.in(2'b11), .out(transistor_11_out), .gate(not_8_out));
  not not_9 (not_9_out, comparator_11_eq);
  Transistor #(.width(2)) transistor_15 (.in(2'b01), .out(transistor_11_out), .gate(not_9_out));
  not not_10 (not_10_out, comparator_12_eq);
  Transistor #(.width(2)) transistor_16 (.in(2'b10), .out(transistor_11_out), .gate(not_10_out));
  not not_11 (not_11_out, comparator_13_eq);
  Transistor #(.width(2)) transistor_17 (.in(2'b01), .out(transistor_11_out), .gate(not_11_out));
  not not_12 (not_12_out, comparator_14_eq);
  Transistor #(.width(2)) transistor_18 (.in(2'b00), .out(transistor_11_out), .gate(not_12_out));
  not not_13 (not_13_out, demultiplexer_2_out1);
  Pull_Resistor pull_resistor_5 (.node(pull_resistor_5_node));
  Multiplexer #(.width(2)) multiplexer_1 (
    .in0(transistor_11_out), .in1(transistor_5_out), .out(pull_resistor_5_node), .sel(not_13_out));
  Pull_Resistor pull_resistor_6 (.node(transistor_11_out[0]));
  Pull_Resistor pull_resistor_7 (.node(transistor_11_out[1]));

  // Notes on the sheet:
  //   var
  //   data
  //   01=new var
  //   10=save data in var
  //   11=out value of var
  //   out
  //   memory adress
endmodule
